# Fritzing sketch Luftdata_pcb_NodeMCU_V1_V2_V3_ADS1115 (saved by Fritzing 0.9.3b)
circuit board: 6.50169cm x 6.99912cm

parts:
  R1 = Resistor [tolerance=±5% resistance=4.7k package=THT]
  J8 = Generic male header - 4 pins [form="♂ (male)" part_number=I2C-5-1 package=THT]
  J4 = Generic male header - 4 pins [form="♂ (male)" part_number=I2C-3-3 package=THT]
  J3 = Generic male header - 4 pins [form="♂ (male)" part_number=I2C-3-1 package=THT]
  J2 = Generic male header - 4 pins [form="♂ (male)" part_number=I2C-3-2 package=THT]
  J7 = Generic male header - 4 pins [form="♂ (male)" part_number=I2C-5-2 package=THT]
  J5 = Generic male header - 4 pins [form="♂ (male)" part_number=I2C-3-4 package=THT]
  J6 = Generic male header - 4 pins [form="♂ (male)" part_number=I2C-3-5 package=THT]
  J9 = Generic male header - 4 pins [form="♂ (male)" part_number=DHT22 package=THT]
  SDS011 = Generic male header - 5 pins [form="♂ (male)" package=THT]
  NodeMCU_V3 = NodeMCU V3.0
  ADS1115 = Adafruit ADS1115 16Bit I2C ADC [part_number="Adafruit #1085"]
  J10 = male pin header, 4 pins [form="♂ (male)"]
  Pad1 = Pad [width=1.9191111111111121 height=1.9191111111111103 connect=center]
  NodeMCU_V1/V2 = NodeMCU V1.0

nets (from the pcb view):
  N1: R1.Pin_0, J9.pin3, NodeMCU_V3.D7, NodeMCU_V1/V2.D7
  3V3: R1.Pin_1, J4.pin1, J3.pin1, J2.pin1, J5.pin1, J6.pin1, J9.pin4, NodeMCU_V3.3V3, ADS1115.VDD, NodeMCU_V1/V2.3V3
  N2: J8.pin1, J7.pin1, SDS011.pin2, NodeMCU_V3.VU, NodeMCU_V1/V2.Vin
  GND: J8.gnd, J4.gnd, J3.gnd, J2.gnd, J7.gnd, J5.gnd, J6.gnd, J9.pin1, SDS011.pin3, NodeMCU_V3.GND, ADS1115.GND, Pad1.pad, NodeMCU_V1/V2.GND
  N3: J8.pin3, J4.pin3, J3.pin3, J2.pin3, J7.pin3, J5.pin3, J6.pin3, NodeMCU_V3.D4, ADS1115.SCL, NodeMCU_V1/V2.D4
  N4: J8.pin4, J4.pin4, J3.pin4, J2.pin4, J7.pin4, J5.pin4, J6.pin4, NodeMCU_V3.D3, ADS1115.SDA, NodeMCU_V1/V2.D3
  N5: SDS011.pin4, NodeMCU_V3.D2, NodeMCU_V1/V2.D2
  N6: SDS011.pin5, NodeMCU_V3.D1, NodeMCU_V1/V2.D1
  N7: NodeMCU_V3.D0, NodeMCU_V1/V2.D0
  N8: NodeMCU_V3.D5, NodeMCU_V1/V2.D5
  N9: NodeMCU_V3.D6, NodeMCU_V1/V2.D6
  N10: NodeMCU_V3.D8, NodeMCU_V1/V2.D8
  N11: NodeMCU_V3.RX, NodeMCU_V1/V2.RX
  N12: NodeMCU_V3.TX, NodeMCU_V1/V2.TX
  N13: NodeMCU_V3.RST, NodeMCU_V1/V2.RST
  N14: NodeMCU_V3.EN, NodeMCU_V1/V2.EN
  N15: NodeMCU_V3.SK, NodeMCU_V1/V2.CLK
  N16: NodeMCU_V3.S0, NodeMCU_V1/V2.SD0
  N17: NodeMCU_V3.SC, NodeMCU_V1/V2.CMD
  N18: NodeMCU_V3.S1, NodeMCU_V1/V2.SD1
  N19: NodeMCU_V3.S2, NodeMCU_V1/V2.SD2
  N20: NodeMCU_V3.S3, NodeMCU_V1/V2.SD3
  N21: NodeMCU_V3.A0, NodeMCU_V1/V2.A0
  N22: ADS1115.AIN3, J10.pin1
  N23: ADS1115.AIN2, J10.pin2
  N24: ADS1115.AIN1, J10.pin3
  N25: ADS1115.AIN0, J10.pin4

notes:
  SDA
  SCL
  GND
  VCC 3.3V
  VCC
  TX
  RX
  VCC 5V
  LUFTDATA.SE
  DAT
  D0
  A0
  A1
  A2
  A3

custom parts:
  Generic male header - 4 pins: Generic male header
  Generic male header - 4 pins: Generic male header
  Generic male header - 5 pins: Generic male header
  NodeMCU V3.0: ESP8266 based NodeMCU
  Adafruit ADS1115 16Bit I2C ADC: For microcontrollers without an analog-to-digital converter or when you want a higher-precision ADC, the ADS1115 provides 16-bit precision at 860 samples/second over I2C. The chip can be configured as 4 single-ended input channels, or two differential channels. As a nice bonus, it even includes a programmable gain amplifier, up to x16, to help boost up smaller single/differential signals to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
  NodeMCU V1.0: ESP8266 based NodeMCU
