# Fritzing sketch Vekotinverstas_pcb_wemos_pro_v2 (saved by Fritzing 0.9.3b)
circuit board: 6.50169cm x 6.99912cm

parts:
  R1 = Resistor [tolerance=±5% resistance=4.7k package=THT]
  J8 = Generic male header - 4 pins [form="♂ (male)" part_number=I2C-5-1 package=THT]
  J4 = Generic male header - 4 pins [form="♂ (male)" part_number=I2C-3-3 package=THT]
  J3 = Generic male header - 4 pins [form="♂ (male)" part_number=I2C-3-1 package=THT]
  J2 = Generic male header - 4 pins [form="♂ (male)" part_number=I2C-3-2 package=THT]
  J7 = Generic male header - 4 pins [form="♂ (male)" part_number=I2C-5-2 package=THT]
  J5 = Generic male header - 4 pins [form="♂ (male)" part_number=I2C-3-4 package=THT]
  J6 = Generic male header - 4 pins [form="♂ (male)" part_number=I2C-3-5 package=THT]
  J9 = Generic male header - 4 pins [form="♂ (male)" part_number=DHT22 package=THT]
  SDS011 = Generic male header - 5 pins [form="♂ (male)" package=THT]
  WeMos_D1_Mini1 = WeMos D1 Mini

nets:
  N1: R1.Pin_0, J9.pin3, WeMos_D1_Mini1.D7
  N2: R1.Pin_1, J4.pin1, J3.pin1, J2.pin1, J5.pin1, J6.pin1, J9.pin4, WeMos_D1_Mini1.3V3
  N3: J8.pin1, J7.pin1, SDS011.pin2, WeMos_D1_Mini1.5V
  GND: J8.gnd, J4.gnd, J3.gnd, J2.gnd, J7.gnd, J5.gnd, J6.gnd, J9.pin1, SDS011.pin3, WeMos_D1_Mini1.G
  N4: J8.pin3, J4.pin3, J3.pin3, J2.pin3, J7.pin3, J5.pin3, J6.pin3, WeMos_D1_Mini1.D4
  N5: J8.pin4, J4.pin4, J3.pin4, J2.pin4, J7.pin4, J5.pin4, J6.pin4, WeMos_D1_Mini1.D3
  N6: SDS011.pin4, WeMos_D1_Mini1.D2
  N7: SDS011.pin5, WeMos_D1_Mini1.D1

notes:
  SDA
  SCL
  GND
  VCC 3.3V
  VCC
  TX
  RX
  VCC 5V
  Vekotinverstas.fi
  DAT
  Wemos D1
  Mini Pro
  v2.0

custom parts:
  Generic male header - 4 pins: Generic male header
  Generic male header - 4 pins: Generic male header
  Generic male header - 5 pins: Generic male header
  WeMos D1 Mini: The D1 mini is a mini wifi board based on ESP-8266EX.
