# Fritzing sketch Luftdata_pcb_ESP12 (saved by Fritzing 0.9.3b)
circuit board: 6.46882cm x 6.99445cm

parts:
  R1 = Resistor [tolerance=±5% resistance=4.7k package=THT]
  J8 = Generic male header - 4 pins [form="♂ (male)" part_number=I2C-5-1 package=THT]
  J4 = Generic male header - 4 pins [form="♂ (male)" part_number=I2C-3-3 package=THT]
  J3 = Generic male header - 4 pins [form="♂ (male)" part_number=I2C-3-1 package=THT]
  J2 = Generic male header - 4 pins [form="♂ (male)" part_number=I2C-3-2 package=THT]
  J7 = Generic male header - 4 pins [form="♂ (male)" part_number=I2C-5-2 package=THT]
  J5 = Generic male header - 4 pins [form="♂ (male)" part_number=I2C-3-4 package=THT]
  J6 = Generic male header - 4 pins [form="♂ (male)" part_number=I2C-3-5 package=THT]
  J9 = Generic male header - 4 pins [form="♂ (male)" part_number=DHT22 package=THT]
  SDS011 = Generic male header - 5 pins [form="♂ (male)" package=THT]
  X1 = USB Connectors [package=usb-microb]
  C1 = Capacitor Polarized [package=cpol-radial-1000uf-25v]
  REG1 = LD33 Low-Dropout Voltage Regulator
  U1 = ESP-12F (ESP8266 WiFi Module) [part_number=ESP8266]
  FTDI = male pin header, 6 pins [form="♂ (male)"]

nets:
  N1: R1.Pin_0, J9.pin3, U1.GPIO13
  N2: R1.Pin_1, J8.pin3, J4.pin1, J4.pin3, J3.pin1, J3.pin3, J2.pin1, J2.pin3, J7.pin3, J5.pin1, J5.pin3, J6.pin1, J6.pin3, J9.pin4, REG1.Vout, U1.VCC, U1.GPIO2, FTDI.pin3
  N3: J8.pin1, J7.pin1, SDS011.pin2, X1.VBUS, C1.+, REG1.Vin
  GND: J8.gnd, J7.gnd, SDS011.pin3, X1.GND, C1.-, REG1.GND
  N4: J8.pin4, J4.pin4, J3.pin4, J2.pin4, J7.pin4, J5.pin4, J6.pin4, U1.GPIO0
  GND_2: J4.gnd, J3.gnd, J2.gnd, J5.gnd, J6.gnd, J9.pin1
  N5: SDS011.pin4, U1.GPIO5
  N6: SDS011.pin5, U1.GPIO4
  N7: U1.RXD0, FTDI.pin5
  N8: U1.GND, U1.GPIO15, FTDI.pin1
  N9: U1.TXD0, FTDI.pin4
  N10: U1.CS0, FTDI.pin2, FTDI.pin6

notes:
  SDA
  SCL
  GND
  VCC 3.3V
  VCC 5V
  LUFTDATA.SE
  VCC
  DAT
  TX
  RX
  CTS
  RTS

custom parts:
  Generic male header - 4 pins: Generic male header
  Generic male header - 4 pins: Generic male header
  Generic male header - 5 pins: Generic male header
  ESP-12F (ESP8266 WiFi Module): WiFi Module based on the ESP8266 with onboard PCB antenna and UART communications
